// Digital circuit Demultiplexador.dig as structural Verilog
module Demultiplexador (
  input  in_1,
  input  C_1,
  input  C_2,
  output S_1,
  output S_2,
  output S_3,
  output S_4
);

  wire and_1_out, and_2_out, and_3_out, and_4_out, not_1_out, not_2_out, not_3_out, not_4_out;

  not not_1 (not_1_out, C_1);
  and and_1 (and_1_out, not_1_out, not_2_out);
  not not_2 (not_2_out, C_2);
  not not_3 (not_3_out, C_1);
  and and_2 (and_2_out, not_3_out, C_2);
  and and_3 (and_3_out, C_1, not_4_out);
  not not_4 (not_4_out, C_2);
  and and_4 (and_4_out, C_1, C_2);
  and and_5 (S_1, and_1_out, in_1);
  and and_6 (S_2, and_2_out, in_1);
  and and_7 (S_3, and_3_out, in_1);
  and and_8 (S_4, and_4_out, in_1);
endmodule
