// Digital circuit Meio_somador.dig as structural Verilog
module Meio_somador (
  input  A,
  input  B,
  output Soma,
  output Carry_out
);

  xor xor_1 (Soma, A, B);
  and and_1 (Carry_out, A, B);
endmodule
