// Digital circuit Meio_subtrador.dig as structural Verilog
module Meio_subtrador (
  input  A,
  input  B,
  output Soma,
  output Carry_out
);

  wire not_1_out;

  xor xor_1 (Soma, A, B);
  not not_1 (not_1_out, A);
  and and_1 (Carry_out, not_1_out, B);
endmodule
