// Digital circuit PRATICA03-p1.dig as structural Verilog
module PRATICA03_p1 (
  input  A,
  input  B,
  input  C,
  input  D
);

  wire and_1_out, and_2_out, and_3_out, or_1_out;

  and and_1 (and_1_out, B, C);
  and and_2 (and_2_out, A, B);
  and and_3 (and_3_out, and_1_out, D);
  or or_1 (or_1_out, and_2_out, and_3_out);
  LED S (.in(or_1_out));

  // Notes on the sheet:
  //   A: JÁ PASSA DAS 17H
  //   B: MÁQUINAS DESLIGADAS
  //   C: É SEXTA
  //   D: PRODUÇÃO DO DIA ATENDIDA
  //   MARLON DUARTE - 493408
endmodule
