// Digital circuit Pretica 2.dig as structural Verilog
module Pretica_2 (
  input  A,
  input  B,
  input  C
);

  wire and_1_out, and_2_out, and_3_out, not_1_out, not_2_out, or_1_out, or_2_out;

  not not_1 (not_1_out, B);
  and and_1 (and_1_out, C, B);
  or or_1 (or_1_out, A, C);
  or or_2 (or_2_out, A, not_1_out);
  and and_2 (and_2_out, and_1_out, or_1_out);
  not not_2 (not_2_out, and_2_out);
  and and_3 (and_3_out, or_2_out, not_2_out);
  LED S (.in(and_3_out));
endmodule
