// Digital circuit pr05_parte1-q2.dig as structural Verilog
module pr05_parte1_q2 (
  input  b_8,
  input  b_7,
  input  b_6,
  input  b_5,
  input  b_4,
  input  b_3,
  input  b_2,
  input  b_1,
  input  a_8,
  input  a_7,
  input  a_6,
  input  a_5,
  input  a_4,
  input  a_3,
  input  a_2,
  input  a_1,
  output s_1,
  output s_2,
  output s_3,
  output s_4,
  output s_5,
  output s_6,
  output s_7,
  output s_8
);

  wire _74283_1_pin9, _74283_2_pin9;

  _74283 _74283_1 (
    .pin1(s_2), .pin2(b_2), .pin3(a_2), .pin4(s_1), .pin5(a_1), .pin6(b_1), .pin7(1'b0), .pin8(1'b0),
    .pin9(_74283_1_pin9), .pin10(s_4), .pin11(b_4), .pin12(a_4), .pin13(s_3), .pin14(a_3), .pin15(b_3),
    .pin16(1'b1));
  _74283 _74283_2 (
    .pin1(s_6), .pin2(b_6), .pin3(a_6), .pin4(s_5), .pin5(a_5), .pin6(b_5), .pin7(_74283_1_pin9),
    .pin8(1'b0), .pin9(_74283_2_pin9), .pin10(s_8), .pin11(b_8), .pin12(a_8), .pin13(s_7), .pin14(a_7),
    .pin15(b_7), .pin16(1'b1));
  LED led_1 (.in(_74283_2_pin9));

  // Notes on the sheet:
  //   MARLON-DUARTE-493408
endmodule
