// Digital circuit pr06_pt01_2.dig as structural Verilog
module pr06_pt01_2 (
  input  Clock
);

  wire _7448_1_pin9, _7448_1_pin10, _7448_1_pin11, _7448_1_pin12, _7448_1_pin13, _7448_1_pin14,
       _7448_1_pin15, _7474_1_pin2, _7474_1_pin5, _7474_1_pin8, _7474_1_pin9, _7474_2_pin2, _7474_2_pin5,
       _7474_2_pin8;

  _7474 _7474_1 (
    .pin1(1'b1), .pin2(_7474_1_pin2), .pin3(Clock), .pin4(1'b1), .pin5(_7474_1_pin5), .pin6(_7474_1_pin2),
    .pin7(1'b0), .pin8(_7474_1_pin8), .pin9(_7474_1_pin9), .pin10(1'b1), .pin11(_7474_1_pin5),
    .pin12(_7474_1_pin8), .pin13(1'b1), .pin14(1'b1));
  _7474 _7474_2 (
    .pin1(1'b1), .pin2(_7474_2_pin2), .pin3(_7474_1_pin9), .pin4(1'b1), .pin5(_7474_2_pin5),
    .pin6(_7474_2_pin2), .pin7(1'b0), .pin8(_7474_2_pin8), .pin10(1'b1), .pin11(_7474_2_pin5),
    .pin12(_7474_2_pin8), .pin13(1'b1), .pin14(1'b1));  // open: pin9
  Seven_Seg #(.ledPersistence("true"), .commonConnectionType("anode")) seven_seg_1 (
    .a(_7448_1_pin13), .b(_7448_1_pin12), .c(_7448_1_pin11), .d(_7448_1_pin10), .e(_7448_1_pin9),
    .f(_7448_1_pin15), .g(_7448_1_pin14), .dp(1'b0));
  _7448 _7448_1 (
    .pin1(_7474_1_pin8), .pin2(_7474_2_pin2), .pin3(1'b1), .pin4(1'b1), .pin5(1'b1), .pin6(1'b0),
    .pin7(_7474_1_pin2), .pin8(1'b0), .pin9(_7448_1_pin9), .pin10(_7448_1_pin10), .pin11(_7448_1_pin11),
    .pin12(_7448_1_pin12), .pin13(_7448_1_pin13), .pin14(_7448_1_pin14), .pin15(_7448_1_pin15), .pin16(1'b1));

  // Notes on the sheet:
  //   MARLON-DUARTE_493408
endmodule
