// Digital circuit pr06_pt02_1_hex.dig as structural Verilog
module pr06_pt02_1_hex (
  input  clk
);

  wire _74m48_1_pin9, _74m48_1_pin10, _74m48_1_pin11, _74m48_1_pin12, _74m48_1_pin13, _74m48_1_pin14,
       _74m48_1_pin15, jk_ff_as_1_nq, jk_ff_as_1_q, jk_ff_as_2_nq, jk_ff_as_2_q, jk_ff_as_3_nq, jk_ff_as_3_q,
       jk_ff_as_4_nq;

  JK_FF_AS jk_ff_as_1 (.Set(1'b0), .J(1'b1), .C(clk), .K(1'b1), .Clr(1'b0), .Q(jk_ff_as_1_q), .nQ(jk_ff_as_1_nq));
  JK_FF_AS jk_ff_as_2 (
    .Set(1'b0), .J(1'b1), .C(jk_ff_as_1_q), .K(1'b1), .Clr(1'b0), .Q(jk_ff_as_2_q), .nQ(jk_ff_as_2_nq));
  JK_FF_AS jk_ff_as_3 (
    .Set(1'b0), .J(1'b1), .C(jk_ff_as_2_q), .K(1'b1), .Clr(1'b0), .Q(jk_ff_as_3_q), .nQ(jk_ff_as_3_nq));
  JK_FF_AS jk_ff_as_4 (.Set(1'b0), .J(1'b1), .C(jk_ff_as_3_q), .K(1'b1), .Clr(1'b0), .nQ(jk_ff_as_4_nq));  // open: Q
  _74M48 _74m48_1 (
    .pin1(jk_ff_as_2_nq), .pin2(jk_ff_as_3_nq), .pin3(1'b1), .pin4(1'b1), .pin5(1'b1), .pin6(jk_ff_as_4_nq),
    .pin7(jk_ff_as_1_nq), .pin8(1'b0), .pin9(_74m48_1_pin9), .pin10(_74m48_1_pin10), .pin11(_74m48_1_pin11),
    .pin12(_74m48_1_pin12), .pin13(_74m48_1_pin13), .pin14(_74m48_1_pin14), .pin15(_74m48_1_pin15),
    .pin16(1'b1));
  Seven_Seg #(.ledPersistence("true"), .commonConnectionType("anode")) seven_seg_1 (
    .a(_74m48_1_pin13), .b(_74m48_1_pin12), .c(_74m48_1_pin11), .d(_74m48_1_pin10), .e(_74m48_1_pin9),
    .f(_74m48_1_pin15), .g(_74m48_1_pin14), .dp(1'b0));

  // Notes on the sheet:
  //   MARLON-DUARTE_493408
endmodule
