// Digital circuit pr06_pt02_2.dig as structural Verilog
module pr06_pt02_2 (
  input  clk,
  input  clk_2
);

  wire _7408_1_pin3, _7408_1_pin4, _7408_1_pin6, _7408_1_pin8, _7408_2_pin3, _7408_2_pin6, _7408_2_pin9,
       _7408_2_pin12, _7448_1_pin9, _7448_1_pin10, _7448_1_pin11, _7448_1_pin12, _7448_1_pin13,
       _7448_1_pin14, _7448_1_pin15, _7448_2_pin9, _7448_2_pin10, _7448_2_pin11, _7448_2_pin12,
       _7448_2_pin13, _7448_2_pin14, _7448_2_pin15, _7476_1_pin3, _7476_1_pin6, _7476_1_pin11, _7476_2_pin6,
       _7476_2_pin11, _7476_3_pin3, _7476_3_pin6, _7476_3_pin11, _7476_4_pin6, _7476_4_pin11, not_1_out;

  _7476 _7476_1 (
    .pin1(clk), .pin2(1'b1), .pin3(_7476_1_pin3), .pin4(1'b1), .pin5(1'b1), .pin6(_7476_1_pin6), .pin7(1'b1),
    .pin8(_7476_1_pin3), .pin9(1'b1), .pin11(_7476_1_pin11), .pin12(1'b1), .pin13(1'b0),
    .pin15(_7476_1_pin6), .pin16(1'b1));  // open: pin10, pin14
  _7476 _7476_2 (
    .pin1(_7476_1_pin11), .pin2(1'b1), .pin3(_7476_1_pin3), .pin4(1'b1), .pin5(1'b1), .pin6(_7476_2_pin6),
    .pin7(1'b1), .pin8(_7476_1_pin3), .pin9(1'b1), .pin11(_7476_2_pin11), .pin12(1'b1), .pin13(1'b0),
    .pin15(_7476_2_pin6), .pin16(1'b1));  // open: pin10, pin14
  not not_1 (not_1_out, _7476_1_pin6);
  _7408 _7408_1 (
    .pin1(not_1_out), .pin2(_7476_1_pin11), .pin3(_7408_1_pin3), .pin4(_7408_1_pin4), .pin5(_7476_2_pin11),
    .pin6(_7408_1_pin6), .pin7(1'b0), .pin8(_7408_1_pin8), .pin9(_7408_1_pin6), .pin10(_7408_1_pin3),
    .pin12(1'b0), .pin13(1'b0), .pin14(1'b1));  // open: pin11
  not not_2 (_7408_1_pin4, _7476_2_pin6);
  _7448 _7448_1 (
    .pin1(_7476_1_pin11), .pin2(_7476_2_pin6), .pin3(1'b1), .pin4(1'b1), .pin5(1'b1), .pin6(_7476_2_pin11),
    .pin7(_7476_1_pin6), .pin8(1'b0), .pin9(_7448_1_pin9), .pin10(_7448_1_pin10), .pin11(_7448_1_pin11),
    .pin12(_7448_1_pin12), .pin13(_7448_1_pin13), .pin14(_7448_1_pin14), .pin15(_7448_1_pin15), .pin16(1'b1));
  not not_3 (_7476_1_pin3, _7408_1_pin8);
  Seven_Seg #(.ledPersistence("true"), .commonConnectionType("anode")) seven_seg_1 (
    .a(_7448_1_pin13), .b(_7448_1_pin12), .c(_7448_1_pin11), .d(_7448_1_pin10), .e(_7448_1_pin9),
    .f(_7448_1_pin15), .g(_7448_1_pin14), .dp(1'b0));
  _7476 _7476_3 (
    .pin1(clk_2), .pin2(1'b1), .pin3(_7476_3_pin3), .pin4(1'b1), .pin5(1'b1), .pin6(_7476_3_pin6),
    .pin7(1'b1), .pin8(_7476_3_pin3), .pin9(1'b1), .pin11(_7476_3_pin11), .pin12(1'b1), .pin13(1'b0),
    .pin15(_7476_3_pin6), .pin16(1'b1));  // open: pin10, pin14
  _7476 _7476_4 (
    .pin1(_7476_3_pin11), .pin2(1'b1), .pin3(_7476_3_pin3), .pin4(1'b1), .pin5(1'b1), .pin6(_7476_4_pin6),
    .pin7(1'b1), .pin8(_7476_3_pin3), .pin9(1'b1), .pin11(_7476_4_pin11), .pin12(1'b1), .pin13(1'b0),
    .pin15(_7476_4_pin6), .pin16(1'b1));  // open: pin10, pin14
  _7408 _7408_2 (
    .pin1(_7476_4_pin11), .pin2(_7476_4_pin6), .pin3(_7408_2_pin3), .pin4(_7476_4_pin11),
    .pin5(_7476_3_pin11), .pin6(_7408_2_pin6), .pin7(1'b0), .pin8(1'b0), .pin9(_7408_2_pin9), .pin10(1'b0),
    .pin11(1'b0), .pin12(_7408_2_pin12), .pin13(_7408_2_pin6), .pin14(_7408_2_pin3));
  _7448 _7448_2 (
    .pin1(_7476_3_pin11), .pin2(_7476_4_pin6), .pin3(1'b1), .pin4(1'b1), .pin5(1'b1), .pin6(_7476_4_pin11),
    .pin7(_7476_3_pin6), .pin8(1'b0), .pin9(_7448_2_pin9), .pin10(_7448_2_pin10), .pin11(_7448_2_pin11),
    .pin12(_7448_2_pin12), .pin13(_7448_2_pin13), .pin14(_7448_2_pin14), .pin15(_7448_2_pin15), .pin16(1'b1));
  not not_4 (_7476_3_pin3, _7408_2_pin12);
  _7432 _7432_1 (
    .pin1(_7408_2_pin3), .pin2(_7408_2_pin6), .pin3(_7408_2_pin12), .pin4(1'b0), .pin5(1'b0),
    .pin6(_7408_2_pin9), .pin7(1'b0), .pin9(1'b1), .pin10(1'b1), .pin12(1'b1), .pin13(1'b1), .pin14(1'b1));  // open: pin8, pin11
  Seven_Seg #(.ledPersistence("true"), .commonConnectionType("anode")) seven_seg_2 (
    .a(_7448_2_pin13), .b(_7448_2_pin12), .c(_7448_2_pin11), .d(_7448_2_pin10), .e(_7448_2_pin9),
    .f(_7448_2_pin15), .g(_7448_2_pin14), .dp(1'b0));

  // Notes on the sheet:
  //   MARLON-DUARTE_493408
  //   MARLON-DUARTE_493409
endmodule
