// Digital circuit Somador_completo.dig as structural Verilog
module Somador_completo (
  input  A,
  input  B,
  input  Carry_in,
  output Soma,
  output Carry_out
);

  wire and_1_out, and_2_out, and_3_out, or_1_out, xor_1_out;

  xor xor_1 (xor_1_out, A, B);
  and and_1 (and_1_out, A, Carry_in);
  and and_2 (and_2_out, A, B);
  and and_3 (and_3_out, B, Carry_in);
  xor xor_2 (Soma, xor_1_out, Carry_in);
  or or_1 (or_1_out, and_1_out, and_2_out);
  or or_2 (Carry_out, or_1_out, and_3_out);
endmodule
