// Digital circuit ATIVIDADE_ENTREGAR_04_.dig as structural Verilog
module ATIVIDADE_ENTREGAR_04 (
  input  B,
  input  A,
  input  C,
  input  D
);

  wire and_1_out, and_2_out, and_3_out, and_4_out, not_1_out, not_2_out, not_3_out, not_4_out, not_5_out,
       or_1_out, or_2_out, or_3_out;

  not not_1 (not_1_out, A);
  not not_2 (not_2_out, C);
  not not_3 (not_3_out, D);
  and and_1 (and_1_out, not_4_out, not_5_out);
  not not_4 (not_4_out, B);
  not not_5 (not_5_out, C);
  and and_2 (and_2_out, B, C);
  and and_3 (and_3_out, not_2_out, not_3_out);
  and and_4 (and_4_out, and_2_out, D);
  or or_1 (or_1_out, not_1_out, and_3_out);
  or or_2 (or_2_out, and_1_out, and_4_out);
  or or_3 (or_3_out, or_1_out, or_2_out);
  LED S (.in(or_3_out));
endmodule
