// Digital circuit Contador_mod5_live_30-10.dig as structural Verilog
module Contador_mod5_live_30_10 (
  input  clk,
  input  clk_2
);

  wire _7476_1_pin6, _7476_1_pin11, _7476_2_pin15, and_1_out, jk_ff_as_1_nq, jk_ff_as_1_q, jk_ff_as_2_nq,
       jk_ff_as_2_q, jk_ff_as_3_nq, not_1_out, not_2_out;

  not not_1 (not_1_out, and_1_out);
  _7476 _7476_1 (
    .pin1(clk_2), .pin2(1'b1), .pin3(not_1_out), .pin4(1'b1), .pin5(1'b1), .pin6(_7476_1_pin6), .pin7(1'b1),
    .pin8(not_1_out), .pin9(1'b1), .pin11(_7476_1_pin11), .pin12(1'b1), .pin13(1'b0), .pin15(_7476_1_pin6),
    .pin16(1'b1));  // open: pin10, pin14
  _7476 _7476_2 (
    .pin1(_7476_1_pin11), .pin2(1'b1), .pin3(not_1_out), .pin4(1'b1), .pin5(1'b1), .pin6(1'b0), .pin7(1'b1),
    .pin8(not_1_out), .pin9(1'b1), .pin12(1'b1), .pin13(1'b0), .pin15(_7476_2_pin15), .pin16(1'b1));  // open: pin10, pin11, pin14
  not not_2 (not_2_out, _7476_1_pin11);
  and and_1 (and_1_out, _7476_2_pin15, not_2_out, _7476_1_pin6);
  LED a_5 (.in(_7476_2_pin15));
  LED a_3 (.in(_7476_1_pin6));
  LED a_4 (.in(_7476_1_pin11));
  JK_FF_AS jk_ff_as_1 (.Set(1'b0), .J(1'b1), .C(clk), .K(1'b1), .Clr(1'b0), .Q(jk_ff_as_1_q), .nQ(jk_ff_as_1_nq));
  LED a_1 (.in(jk_ff_as_2_nq));
  LED a_2 (.in(jk_ff_as_3_nq));
  LED a_0 (.in(jk_ff_as_1_nq));
  JK_FF_AS jk_ff_as_2 (
    .Set(1'b0), .J(1'b1), .C(jk_ff_as_1_q), .K(1'b1), .Clr(1'b0), .Q(jk_ff_as_2_q), .nQ(jk_ff_as_2_nq));
  JK_FF_AS jk_ff_as_3 (.Set(1'b0), .J(1'b1), .C(jk_ff_as_2_q), .K(1'b1), .Clr(1'b0), .nQ(jk_ff_as_3_nq));  // open: Q
endmodule
