// Digital circuit Multiplexador.dig as structural Verilog
module Multiplexador (
  input  C1,
  input  C2,
  input  In_3,
  input  In_4,
  input  In_1,
  input  In_2,
  output \Saída 
);

  wire and_1_out, and_2_out, and_3_out, and_4_out, and_5_out, and_6_out, and_7_out, and_8_out, not_1_out,
       not_2_out, not_3_out, not_4_out, or_1_out, or_2_out;

  not not_1 (not_1_out, C1);
  not not_2 (not_2_out, C2);
  not not_3 (not_3_out, C1);
  not not_4 (not_4_out, C2);
  and and_1 (and_1_out, not_1_out, not_2_out);
  and and_2 (and_2_out, not_3_out, C2);
  and and_3 (and_3_out, C1, not_4_out);
  and and_4 (and_4_out, C1, C2);
  and and_5 (and_5_out, and_1_out, In_1);
  and and_6 (and_6_out, and_2_out, In_2);
  and and_7 (and_7_out, and_3_out, In_3);
  and and_8 (and_8_out, and_4_out, In_4);
  or or_1 (or_1_out, and_5_out, and_6_out);
  or or_2 (or_2_out, and_7_out, and_8_out);
  or or_3 (\Saída , or_1_out, or_2_out);
endmodule
