// Digital circuit Multiplexador_CI.dig as structural Verilog
module Multiplexador_CI (
  input  B_1,
  input  B_2,
  input  B_3,
  input  C_0,
  output S_0,
  output S_1,
  output S_2,
  output S_3,
  output S_4,
  output S_5,
  output S_6,
  output S_7
);

  _74138 _74138_1 (
    .pin1(B_1), .pin2(B_2), .pin3(B_3), .pin4(1'b0), .pin5(1'b0), .pin6(C_0), .pin7(S_7), .pin8(1'b0),
    .pin9(S_6), .pin10(S_5), .pin11(S_4), .pin12(S_3), .pin13(S_2), .pin14(S_1), .pin15(S_0), .pin16(1'b1));
endmodule
