// Digital circuit PRATICA03-p1-NOR-NAND.dig as structural Verilog
module PRATICA03_p1_NOR_NAND (
  input  A,
  input  B,
  input  C,
  input  D,
  input  A_2,
  input  B_2,
  input  C_2,
  input  D_2
);

  wire nand_1_out, nand_2_out, nand_3_out, nand_4_out, nand_5_out, nand_6_out, nand_7_out, nand_8_out,
       nand_9_out, nor_1_out, nor_2_out, nor_3_out, nor_4_out, nor_5_out, nor_6_out, nor_7_out, nor_8_out,
       nor_9_out, nor_10_out, nor_11_out;

  nand nand_1 (nand_1_out, A, B);
  nand nand_2 (nand_2_out, B, C);
  nor nor_1 (nor_1_out, A_2, A_2);
  nor nor_2 (nor_2_out, B_2, B_2);
  nor nor_3 (nor_3_out, B_2, B_2);
  nor nor_4 (nor_4_out, C_2, C_2);
  nand nand_3 (nand_3_out, nand_1_out, nand_1_out);
  nand nand_4 (nand_4_out, nand_2_out, nand_2_out);
  nor nor_5 (nor_5_out, nor_1_out, nor_2_out);
  nor nor_6 (nor_6_out, nor_3_out, nor_4_out);
  nand nand_5 (nand_5_out, nand_4_out, D);
  nor nor_7 (nor_7_out, nor_6_out, nor_6_out);
  nor nor_8 (nor_8_out, D_2, D_2);
  nand nand_6 (nand_6_out, nand_5_out, nand_5_out);
  nor nor_9 (nor_9_out, nor_7_out, nor_8_out);
  nand nand_7 (nand_7_out, nand_3_out, nand_3_out);
  nand nand_8 (nand_8_out, nand_6_out, nand_6_out);
  nor nor_10 (nor_10_out, nor_5_out, nor_9_out);
  nand nand_9 (nand_9_out, nand_7_out, nand_8_out);
  nor nor_11 (nor_11_out, nor_10_out, nor_10_out);
  LED led_1 (.in(nand_9_out));
  LED led_2 (.in(nor_11_out));

  // Notes on the sheet:
  //   A: JÁ PASSA DAS 17H
  //   B: MÁQUINAS DESLIGADAS
  //   C: É SEXTA
  //   D: PRODUÇÃO DO DIA ATENDIDA
  //   A_2: JÁ PASSA DAS 17H
  //   B_2: MÁQUINAS DESLIGADAS
  //   C_2: É SEXTA
  //   D_2: PRODUÇÃO DO DIA ATENDIDA
  //   MARLON DUARTE - 493408
endmodule
