// Digital circuit PRATICA03_P2_E2_NAND-NOR.dig as structural Verilog
module PRATICA03_P2_E2_NAND_NOR (
  input  X1,
  input  X2,
  input  X3
);

  wire nand_1_out, nand_2_out, nand_3_out, nand_4_out, nand_5_out, nand_6_out, nand_7_out, nand_8_out,
       nand_9_out, nand_10_out, nand_11_out, nand_12_out, nand_13_out, nand_14_out, nand_15_out, nand_16_out,
       nand_17_out, nand_18_out, nand_19_out, nand_20_out, nand_21_out, nand_22_out, nand_23_out, nor_1_out,
       nor_2_out, nor_3_out, nor_4_out, nor_5_out, nor_6_out, nor_7_out, nor_8_out, nor_9_out, nor_10_out,
       nor_11_out, nor_12_out, nor_13_out, nor_14_out, nor_15_out, nor_16_out, nor_17_out, nor_18_out,
       nor_19_out, nor_20_out, nor_21_out, nor_22_out, nor_23_out, nor_24_out, nor_25_out;

  nand nand_1 (nand_1_out, X2, X2);
  nand nand_2 (nand_2_out, X2, X2);
  nand nand_3 (nand_3_out, X1, X1);
  nand nand_4 (nand_4_out, X3, X3);
  nor nor_1 (nor_1_out, X2, X2);
  nor nor_2 (nor_2_out, X2, X2);
  nor nor_3 (nor_3_out, X1, X1);
  nor nor_4 (nor_4_out, X3, X3);
  nand nand_5 (nand_5_out, X1, nand_1_out);
  nand nand_6 (nand_6_out, X1, X3);
  nand nand_7 (nand_7_out, nand_2_out, X3);
  nand nand_8 (nand_8_out, nand_3_out, X2);
  nor nor_5 (nor_5_out, X1, X1);
  nor nor_6 (nor_6_out, nor_1_out, nor_1_out);
  nor nor_7 (nor_7_out, X1, X1);
  nor nor_8 (nor_8_out, X3, X3);
  nor nor_9 (nor_9_out, nor_2_out, nor_2_out);
  nor nor_10 (nor_10_out, X3, X3);
  nor nor_11 (nor_11_out, nor_3_out, nor_3_out);
  nor nor_12 (nor_12_out, X2, X2);
  nand nand_9 (nand_9_out, nand_5_out, nand_5_out);
  nand nand_10 (nand_10_out, nand_6_out, nand_6_out);
  nand nand_11 (nand_11_out, nand_7_out, nand_7_out);
  nand nand_12 (nand_12_out, nand_8_out, nand_8_out);
  nor nor_13 (nor_13_out, nor_5_out, nor_6_out);
  nor nor_14 (nor_14_out, nor_7_out, nor_8_out);
  nor nor_15 (nor_15_out, nor_9_out, nor_10_out);
  nor nor_16 (nor_16_out, nor_11_out, nor_12_out);
  nand nand_13 (nand_13_out, nand_12_out, nand_4_out);
  nand nand_14 (nand_14_out, nand_9_out, nand_9_out);
  nand nand_15 (nand_15_out, nand_10_out, nand_10_out);
  nor nor_17 (nor_17_out, nor_16_out, nor_16_out);
  nor nor_18 (nor_18_out, nor_4_out, nor_4_out);
  nand nand_16 (nand_16_out, nand_14_out, nand_15_out);
  nand nand_17 (nand_17_out, nand_13_out, nand_13_out);
  nor nor_19 (nor_19_out, nor_13_out, nor_14_out);
  nor nor_20 (nor_20_out, nor_17_out, nor_18_out);
  nand nand_18 (nand_18_out, nand_11_out, nand_11_out);
  nand nand_19 (nand_19_out, nand_17_out, nand_17_out);
  nand nand_20 (nand_20_out, nand_18_out, nand_19_out);
  nor nor_21 (nor_21_out, nor_19_out, nor_19_out);
  nor nor_22 (nor_22_out, nor_15_out, nor_20_out);
  nand nand_21 (nand_21_out, nand_16_out, nand_16_out);
  nand nand_22 (nand_22_out, nand_20_out, nand_20_out);
  nor nor_23 (nor_23_out, nor_22_out, nor_22_out);
  nor nor_24 (nor_24_out, nor_21_out, nor_23_out);
  nand nand_23 (nand_23_out, nand_21_out, nand_22_out);
  nor nor_25 (nor_25_out, nor_24_out, nor_24_out);
  LED led_1 (.in(nand_23_out));
  LED led_2 (.in(nor_25_out));

  // Notes on the sheet:
  //   MARLON DUARTE - 493408
endmodule
