// Digital circuit PRATICA03_P2_E3_NAND-NOR.dig as structural Verilog
module PRATICA03_P2_E3_NAND_NOR (
  input  X1,
  input  X2,
  input  X3
);

  wire nand_1_out, nand_2_out, nand_3_out, nand_4_out, nand_5_out, nand_6_out, nand_7_out, nand_8_out,
       nand_9_out, nor_1_out, nor_2_out, nor_3_out, nor_4_out, nor_5_out, nor_6_out, nor_7_out, nor_8_out,
       nor_9_out, nor_10_out;

  nand nand_1 (nand_1_out, X3, X3);
  nand nand_2 (nand_2_out, X1, X1);
  nor nor_1 (nor_1_out, X3, X3);
  nor nor_2 (nor_2_out, X1, X1);
  nand nand_3 (nand_3_out, X1, nand_1_out);
  nand nand_4 (nand_4_out, nand_2_out, X3);
  nor nor_3 (nor_3_out, X1, X1);
  nor nor_4 (nor_4_out, nor_1_out, nor_1_out);
  nor nor_5 (nor_5_out, nor_2_out, nor_2_out);
  nor nor_6 (nor_6_out, X3, X3);
  nand nand_5 (nand_5_out, nand_3_out, nand_3_out);
  nand nand_6 (nand_6_out, nand_4_out, nand_4_out);
  nor nor_7 (nor_7_out, nor_3_out, nor_4_out);
  nor nor_8 (nor_8_out, nor_5_out, nor_6_out);
  nand nand_7 (nand_7_out, nand_5_out, nand_5_out);
  nand nand_8 (nand_8_out, nand_6_out, nand_6_out);
  nor nor_9 (nor_9_out, nor_7_out, nor_8_out);
  nand nand_9 (nand_9_out, nand_7_out, nand_8_out);
  nor nor_10 (nor_10_out, nor_9_out, nor_9_out);
  LED led_1 (.in(nand_9_out));
  LED led_2 (.in(nor_10_out));

  // Notes on the sheet:
  //   MARLON DUARTE - 493408
endmodule
