// Digital circuit PRATICA03_p1.dig as structural Verilog
module PRATICA03_p1 (
  input  X1,
  input  X2,
  input  X3
);

  wire and_1_out, and_2_out, and_3_out, and_4_out, and_5_out, and_6_out, and_7_out, and_8_out, and_9_out,
       and_10_out, and_11_out, not_1_out, not_2_out, not_3_out, not_4_out, not_5_out, not_6_out, not_7_out,
       not_8_out, not_9_out, not_10_out, or_1_out, or_2_out, or_3_out, or_4_out, or_5_out, or_6_out, or_7_out;

  not not_1 (not_1_out, X1);
  not not_2 (not_2_out, X3);
  not not_3 (not_3_out, X1);
  not not_4 (not_4_out, X1);
  not not_5 (not_5_out, X1);
  not not_6 (not_6_out, X2);
  not not_7 (not_7_out, X3);
  not not_8 (not_8_out, X2);
  not not_9 (not_9_out, X2);
  and and_1 (and_1_out, not_1_out, X2);
  not not_10 (not_10_out, X3);
  and and_2 (and_2_out, X1, not_2_out);
  and and_3 (and_3_out, not_3_out, X3);
  and and_4 (and_4_out, not_4_out, X3);
  and and_5 (and_5_out, not_5_out, X2);
  and and_6 (and_6_out, not_6_out, X3);
  and and_7 (and_7_out, X2, not_7_out);
  and and_8 (and_8_out, X1, not_8_out);
  and and_9 (and_9_out, X1, X3);
  and and_10 (and_10_out, not_9_out, X3);
  and and_11 (and_11_out, and_1_out, not_10_out);
  or or_1 (or_1_out, and_2_out, and_3_out);
  or or_2 (or_2_out, and_4_out, and_5_out);
  or or_3 (or_3_out, and_6_out, and_7_out);
  or or_4 (or_4_out, and_8_out, and_9_out);
  or or_5 (or_5_out, and_10_out, and_11_out);
  or or_6 (or_6_out, or_4_out, or_5_out);
  or or_7 (or_7_out, or_2_out, or_3_out);
  LED E1 (.in(or_7_out));
  LED E2 (.in(or_6_out));
  LED E3 (.in(or_1_out));

  // Notes on the sheet:
  //   MARLON DUARTE - 493408
endmodule
