// Digital circuit pr05_parte1-q1.dig as structural Verilog
module pr05_parte1_q1 (
  input  A,
  input  B,
  input  C,
  input  D,
  input  A_2,
  input  B_2,
  input  C_2,
  input  D_2
);

  wire _7448_1_pin9, _7448_1_pin10, _7448_1_pin11, _7448_1_pin12, _7448_1_pin13, _7448_1_pin14,
       _7448_1_pin15, _7448_2_pin9, _7448_2_pin10, _7448_2_pin11, _7448_2_pin12, _7448_2_pin13,
       _7448_2_pin14, _7448_2_pin15, _7448_3_pin9, _7448_3_pin10, _7448_3_pin11, _7448_3_pin12,
       _7448_3_pin13, _7448_3_pin14, _7448_3_pin15, _74283_1_pin1, _74283_1_pin4, _74283_1_pin9,
       _74283_1_pin10, _74283_1_pin13, and_1_out, and_2_out, or_1_out, or_2_out;

  Seven_Seg #(.ledPersistence("true"), .commonConnectionType("anode")) seven_seg_1 (
    .a(_7448_1_pin13), .b(_7448_1_pin12), .c(_7448_1_pin11), .d(_7448_1_pin10), .e(_7448_1_pin9),
    .f(_7448_1_pin15), .g(_7448_1_pin14), .dp(1'b0));
  _7448 _7448_1 (
    .pin1(B), .pin2(C), .pin3(1'b1), .pin4(1'b1), .pin5(1'b1), .pin6(D), .pin7(A), .pin8(1'b0),
    .pin9(_7448_1_pin9), .pin10(_7448_1_pin10), .pin11(_7448_1_pin11), .pin12(_7448_1_pin12),
    .pin13(_7448_1_pin13), .pin14(_7448_1_pin14), .pin15(_7448_1_pin15), .pin16(1'b1));
  _74283 _74283_1 (
    .pin1(_74283_1_pin1), .pin2(B_2), .pin3(B), .pin4(_74283_1_pin4), .pin5(A), .pin6(A_2), .pin7(1'b0),
    .pin8(1'b0), .pin9(_74283_1_pin9), .pin10(_74283_1_pin10), .pin11(D_2), .pin12(D),
    .pin13(_74283_1_pin13), .pin14(C), .pin15(C_2), .pin16(1'b1));
  Seven_Seg #(.ledPersistence("true"), .commonConnectionType("anode")) seven_seg_2 (
    .a(_7448_2_pin13), .b(_7448_2_pin12), .c(_7448_2_pin11), .d(_7448_2_pin10), .e(_7448_2_pin9),
    .f(_7448_2_pin15), .g(_7448_2_pin14), .dp(1'b0));
  _7448 _7448_2 (
    .pin1(B_2), .pin2(C_2), .pin3(1'b1), .pin4(1'b1), .pin5(1'b1), .pin6(D_2), .pin7(A_2), .pin8(1'b0),
    .pin9(_7448_2_pin9), .pin10(_7448_2_pin10), .pin11(_7448_2_pin11), .pin12(_7448_2_pin12),
    .pin13(_7448_2_pin13), .pin14(_7448_2_pin14), .pin15(_7448_2_pin15), .pin16(1'b1));
  _7448 _7448_3 (
    .pin1(_74283_1_pin1), .pin2(_74283_1_pin13), .pin3(1'b1), .pin4(1'b1), .pin5(1'b1),
    .pin6(_74283_1_pin10), .pin7(_74283_1_pin4), .pin8(1'b0), .pin9(_7448_3_pin9), .pin10(_7448_3_pin10),
    .pin11(_7448_3_pin11), .pin12(_7448_3_pin12), .pin13(_7448_3_pin13), .pin14(_7448_3_pin14),
    .pin15(_7448_3_pin15), .pin16(1'b1));
  Seven_Seg #(.ledPersistence("true"), .commonConnectionType("anode")) seven_seg_3 (
    .a(_7448_3_pin13), .b(_7448_3_pin12), .c(_7448_3_pin11), .d(_7448_3_pin10), .e(_7448_3_pin9),
    .f(_7448_3_pin15), .g(_7448_3_pin14), .dp(1'b0));
  Seven_Seg #(.ledPersistence("true"), .commonConnectionType("anode")) seven_seg_4 (
    .a(or_1_out), .b(or_1_out), .c(or_1_out), .d(or_1_out), .e(or_1_out), .f(or_1_out), .g(1'b0), .dp(1'b0));
  or or_1 (or_1_out, _74283_1_pin9, or_2_out);
  or or_2 (or_2_out, and_1_out, and_2_out);
  and and_1 (and_1_out, _74283_1_pin10, _74283_1_pin13);
  Seven_Seg #(.ledPersistence("true"), .commonConnectionType("anode")) seven_seg_5 (
    .a(1'b0), .b(or_1_out), .c(or_1_out), .d(or_1_out), .e(or_1_out), .f(or_1_out), .g(1'b0), .dp(1'b0));
  and and_2 (and_2_out, _74283_1_pin10, _74283_1_pin1);
  Seven_Seg #(.ledPersistence("true"), .commonConnectionType("anode")) seven_seg_6 (
    .a(or_1_out), .b(1'b0), .c(1'b0), .d(or_1_out), .e(or_1_out), .f(or_1_out), .g(or_1_out), .dp(1'b0));
  Seven_Seg #(.ledPersistence("true"), .commonConnectionType("anode")) seven_seg_7 (
    .a(or_1_out), .b(or_1_out), .c(or_1_out), .d(1'b0), .e(or_1_out), .f(or_1_out), .g(or_1_out), .dp(1'b0));

  // Notes on the sheet:
  //   +
  //   =
  //   MARLON-DUARTE-493408
endmodule
