// Digital circuit pr05_parte2-q1.dig as structural Verilog
module pr05_parte2_q1 (
  input  b_0,
  input  a_4,
  input  a_3,
  input  a_2,
  input  a_1,
  input  b_1,
  input  b_2,
  input  b_3
);

  wire m_0, m_1, m_2;

  _7485 _7485_1 (
    .pin1(b_3), .pin2(1'b0), .pin3(1'b1), .pin4(1'b0), .pin5(m_2), .pin6(m_1), .pin7(m_0), .pin8(1'b0),
    .pin9(b_0), .pin10(a_1), .pin11(b_1), .pin12(a_2), .pin13(a_3), .pin14(b_2), .pin15(a_4), .pin16(1'b1));
  LED led_1 (.in(m_0));
  LED led_2 (.in(m_1));
  LED led_3 (.in(m_2));

  // Notes on the sheet:
  //   A
  //   MARLON-DUARTE-493408
  //   <
  //   =
  //   >
  //   B
endmodule
