// Digital circuit pr05_posLab-q2.dig as structural Verilog
module pr05_posLab_q2 (
  input  A_0,
  input  A_1,
  input  A_2,
  input  S_0,
  output B_0,
  output B_1,
  output B_2,
  output B_3
);

  wire and_1_out, and_2_out, and_3_out, and_4_out, and_5_out, and_6_out, and_7_out, and_8_out, and_9_out,
       and_10_out, and_11_out, not_1_out, not_2_out, not_3_out, not_4_out, not_5_out, not_6_out, not_7_out,
       not_8_out, or_1_out, or_2_out, or_3_out;

  not not_1 (not_1_out, S_0);
  not not_2 (not_2_out, A_2);
  not not_3 (not_3_out, A_2);
  not not_4 (not_4_out, A_1);
  not not_5 (not_5_out, A_0);
  not not_6 (not_6_out, S_0);
  not not_7 (not_7_out, A_1);
  and and_1 (and_1_out, not_1_out, A_2);
  and and_2 (and_2_out, S_0, not_2_out);
  and and_3 (and_3_out, S_0, not_3_out);
  and and_4 (and_4_out, A_2, not_4_out);
  and and_5 (and_5_out, A_1, not_5_out);
  and and_6 (and_6_out, not_6_out, A_1);
  and and_7 (and_7_out, S_0, not_7_out);
  not not_8 (not_8_out, A_0);
  and and_8 (and_8_out, and_2_out, A_0);
  and and_9 (and_9_out, and_3_out, A_1);
  and and_10 (and_10_out, and_4_out, not_8_out);
  or or_1 (or_1_out, and_5_out, and_6_out);
  and and_11 (and_11_out, and_7_out, A_0);
  or or_2 (or_2_out, and_1_out, and_8_out);
  or or_3 (or_3_out, and_9_out, and_10_out);
  or or_4 (B_1, or_1_out, and_11_out);
  or or_5 (B_2, or_2_out, or_3_out);

  assign B_0 = A_0;
  assign B_3 = S_0;

  // Notes on the sheet:
  //   MARLON-DUARTE-493408
endmodule
