// Digital circuit pr06_pt02_1.dig as structural Verilog
module pr06_pt02_1 (
  input  clk
);

  wire _7448_1_pin9, _7448_1_pin10, _7448_1_pin11, _7448_1_pin12, _7448_1_pin13, _7448_1_pin14,
       _7448_1_pin15, and_1_out, and_2_out, and_3_out, jk_ff_as_1_nq, jk_ff_as_1_q, jk_ff_as_2_nq,
       jk_ff_as_2_q, jk_ff_as_3_nq, jk_ff_as_3_q, jk_ff_as_4_nq, not_1_out, not_2_out;

  JK_FF_AS jk_ff_as_1 (
    .Set(and_1_out), .J(1'b1), .C(clk), .K(1'b1), .Clr(and_1_out), .Q(jk_ff_as_1_q), .nQ(jk_ff_as_1_nq));
  and and_1 (and_1_out, and_3_out, and_2_out);
  and and_2 (and_2_out, jk_ff_as_2_nq, not_1_out);
  and and_3 (and_3_out, jk_ff_as_4_nq, not_2_out);
  JK_FF_AS jk_ff_as_2 (
    .Set(and_1_out), .J(1'b1), .C(jk_ff_as_1_q), .K(1'b1), .Clr(and_1_out), .Q(jk_ff_as_2_q),
    .nQ(jk_ff_as_2_nq));
  not not_1 (not_1_out, jk_ff_as_1_nq);
  not not_2 (not_2_out, jk_ff_as_3_nq);
  JK_FF_AS jk_ff_as_3 (
    .Set(and_1_out), .J(1'b1), .C(jk_ff_as_2_q), .K(1'b1), .Clr(and_1_out), .Q(jk_ff_as_3_q),
    .nQ(jk_ff_as_3_nq));
  JK_FF_AS jk_ff_as_4 (
    .Set(and_1_out), .J(1'b1), .C(jk_ff_as_3_q), .K(1'b1), .Clr(and_1_out), .nQ(jk_ff_as_4_nq));  // open: Q
  _7448 _7448_1 (
    .pin1(jk_ff_as_2_nq), .pin2(jk_ff_as_3_nq), .pin3(1'b1), .pin4(1'b1), .pin5(1'b1), .pin6(jk_ff_as_4_nq),
    .pin7(jk_ff_as_1_nq), .pin8(1'b0), .pin9(_7448_1_pin9), .pin10(_7448_1_pin10), .pin11(_7448_1_pin11),
    .pin12(_7448_1_pin12), .pin13(_7448_1_pin13), .pin14(_7448_1_pin14), .pin15(_7448_1_pin15), .pin16(1'b1));
  Seven_Seg #(.ledPersistence("true"), .commonConnectionType("anode")) seven_seg_1 (
    .a(_7448_1_pin13), .b(_7448_1_pin12), .c(_7448_1_pin11), .d(_7448_1_pin10), .e(_7448_1_pin9),
    .f(_7448_1_pin15), .g(_7448_1_pin14), .dp(1'b0));

  // Notes on the sheet:
  //   MARLON-DUARTE_493408
endmodule
