// Digital circuit Pr_07_.dig as structural Verilog
module Pr_07 (
  input  [7:0] A_01234567,
  input  [7:0] B_01234567,
  input  M,
  input  Cn,
  input  [3:0] S_0123
);

  wire _74181_2_pin7, undriven, undriven_2, undriven_3, undriven_6, undriven_7, undriven_8;
  wire [0:0] undriven_5;
  wire [3:0] _74181_1_pin1, _74181_2_pin9, not_1_out, not_2_out, not_3_out, not_4_out, not_6_out, undriven_4;

  assign not_1_out = ~A_01234567[7:4];  // Not not_1, 4 bits wide
  assign not_2_out = ~A_01234567[3:0];  // Not not_2, 4 bits wide
  assign not_3_out = ~undriven_4;  // Not not_3, 4 bits wide
  Seven_Seg_Hex seven_seg_hex_1 (.d(A_01234567[7:4]), .dp(1'b0));
  Seven_Seg_Hex seven_seg_hex_2 (.d(A_01234567[3:0]), .dp(1'b0));
  _74181 _74181_1 (
    .pin1(_74181_1_pin1[0]), .pin2(not_2_out[0]), .pin3(S_0123[3]), .pin4(S_0123[2]), .pin5(S_0123[1]),
    .pin6(S_0123[0]), .pin7(Cn), .pin8(M), .pin9(undriven_4[0]), .pin10(undriven_4[1]),
    .pin11(undriven_4[2]), .pin12(1'b0));  // open: pin13, pin14, pin15, pin16, pin17, pin18, pin19, pin20, pin21, pin22, pin23, pin24
  assign not_4_out = ~B_01234567[7:4];  // Not not_4, 4 bits wide
  Seven_Seg_Hex seven_seg_hex_3 (.d(B_01234567[7:4]), .dp(1'b0));
  assign _74181_1_pin1 = ~B_01234567[3:0];  // Not not_5, 4 bits wide
  LED led_1 (.in(undriven));
  LED led_2 (.in(undriven_2));
  LED led_3 (.in(undriven_3));
  Seven_Seg_Hex seven_seg_hex_4 (.d(B_01234567[3:0]), .dp(1'b0));
  assign not_6_out = ~_74181_2_pin9;  // Not not_6, 4 bits wide
  _74181 _74181_2 (
    .pin1(not_4_out[0]), .pin2(not_1_out[0]), .pin3(S_0123[3]), .pin4(S_0123[2]), .pin5(S_0123[1]),
    .pin6(S_0123[0]), .pin7(_74181_2_pin7), .pin8(M), .pin9(_74181_2_pin9[0]), .pin10(_74181_2_pin9[1]),
    .pin11(_74181_2_pin9[2]), .pin12(1'b0));  // open: pin13, pin14, pin15, pin16, pin17, pin18, pin19, pin20, pin21, pin22, pin23, pin24
  Seven_Seg_Hex seven_seg_hex_5 (.d({3'b000, undriven_5[0]}), .dp(1'b0));
  Seven_Seg_Hex seven_seg_hex_6 (.d(not_6_out), .dp(1'b0));
  Seven_Seg_Hex seven_seg_hex_7 (.d(not_3_out), .dp(1'b0));
  LED led_4 (.in(undriven_6));
  LED led_5 (.in(undriven_7));
  LED led_6 (.in(undriven_8));

  // Other names for the same wires on the sheet: M_0 = M

  // Notes on the sheet:
  //   MARLON-DUARTE_493408
endmodule
