// Digital circuit pr07.dig as structural Verilog
module pr07 (
  input  [3:0] A,
  input  [3:0] B,
  input  [3:0] S,
  input  C,
  input  M
);

  wire undriven, undriven_3, undriven_4;
  wire [0:0] undriven_2;
  wire [3:0] _74181_1_pin1, _74181_1_pin2, _74181_1_pin9, not_1_out;

  Seven_Seg_Hex seven_seg_hex_1 (.d({3'b000, undriven_2[0]}), .dp(1'b0));
  Seven_Seg_Hex seven_seg_hex_2 (.d(not_1_out), .dp(1'b0));
  assign not_1_out = ~_74181_1_pin9;  // Not not_1, 4 bits wide
  _74181 _74181_1 (
    .pin1(_74181_1_pin1[0]), .pin2(_74181_1_pin2[0]), .pin3(S[3]), .pin4(S[2]), .pin5(S[1]), .pin6(S[0]),
    .pin7(C), .pin8(M), .pin9(_74181_1_pin9[0]), .pin10(_74181_1_pin9[1]), .pin11(_74181_1_pin9[2]),
    .pin12(1'b0));  // open: pin13, pin14, pin15, pin16, pin17, pin18, pin19, pin20, pin21, pin22, pin23, pin24
  Seven_Seg_Hex seven_seg_hex_3 (.d(A), .dp(1'b0));
  assign _74181_1_pin2 = ~A;  // Not not_2, 4 bits wide
  Seven_Seg_Hex seven_seg_hex_4 (.d(B), .dp(1'b0));
  assign _74181_1_pin1 = ~B;  // Not not_3, 4 bits wide
  LED led_1 (.in(undriven));
  LED led_2 (.in(undriven_3));
  LED led_3 (.in(undriven_4));
endmodule
