// Digital circuit Subtrador_completo.dig as structural Verilog
module Subtrador_completo (
  input  A,
  input  B,
  input  Carry_in,
  output Soma,
  output Carry_out
);

  wire and_1_out, and_2_out, and_3_out, not_1_out, not_2_out, or_1_out, xor_1_out;

  not not_1 (not_1_out, A);
  xor xor_1 (xor_1_out, A, B);
  not not_2 (not_2_out, A);
  and and_1 (and_1_out, not_2_out, Carry_in);
  and and_2 (and_2_out, not_1_out, B);
  and and_3 (and_3_out, B, Carry_in);
  xor xor_2 (Soma, xor_1_out, Carry_in);
  or or_1 (or_1_out, and_1_out, and_2_out);
  or or_2 (Carry_out, or_1_out, and_3_out);
endmodule
