// Digital circuit pr06_p3.dig as structural Verilog
module pr06_p3 (
  input  clk
);

  wire jk_ff_as_1_nq, jk_ff_as_1_q, jk_ff_as_2_nq, jk_ff_as_2_q, jk_ff_as_3_nq;

  JK_FF_AS jk_ff_as_1 (.Set(1'b0), .J(1'b1), .C(clk), .K(1'b1), .Clr(1'b0), .Q(jk_ff_as_1_q), .nQ(jk_ff_as_1_nq));
  LED a_1 (.in(jk_ff_as_2_nq));
  LED a_2 (.in(jk_ff_as_3_nq));
  LED a_0 (.in(jk_ff_as_1_nq));
  JK_FF_AS jk_ff_as_2 (
    .Set(1'b0), .J(1'b1), .C(jk_ff_as_1_q), .K(1'b1), .Clr(1'b0), .Q(jk_ff_as_2_q), .nQ(jk_ff_as_2_nq));
  JK_FF_AS jk_ff_as_3 (.Set(1'b0), .J(1'b1), .C(jk_ff_as_2_q), .K(1'b1), .Clr(1'b0), .nQ(jk_ff_as_3_nq));  // open: Q
endmodule
